# Fritzing sketch Fritzing Sketch Source File (saved by Fritzing 0.9.3b)
breadboards: 1

parts:
  Part1 = Arduino Uno (Rev3) - ICSP
  LED1 = smd LED [color="Red (633nm)" package="1206 [SMD]"]
  R1 = Resistor [tolerance=±5% resistance=220 package="2512 [SMD]"]
  J1 = Piezo Speaker
  J2 = Basic Servo
  HC-SR04_Sensor_1 = HC-SR04 Ultrasonic Distance Sensor

nets:
  GND: Part1.GND, R1.Pin_0, J1.pin2, J2.gnd, HC-SR04_Sensor_1.GND
  N1: Part1.D8, J1.pin1
  N2: Part1.D12/MISO, HC-SR04_Sensor_1.ECHO
  N3: Part1.D13/SCK, HC-SR04_Sensor_1.TRIG
  N4: Part1.D4, LED1.cathode, R1.Pin_1
  N5: Part1.D5_PWM, J2.pulse
  VCC: Part1.5V, J2.vcc, HC-SR04_Sensor_1.VCC

notes:
  Developed By Web Dev Fusion
  https://www.webdevfusion.com
  Developed By Web Dev Fusion
  www.webdevfusion.com
  GND - Green
  5VC - Red
  GPIO - Blue
